# Fritzing sketch Circuit (saved by Fritzing 0.9.3b)
breadboards: 1

parts:
  Arduino = Arduino Uno (Rev3)
  Wrist = Basic Servo
  Elbow = Basic Servo
  ccwShoulder = Basic Servo
  cwShoulder = Basic Servo
  Gripper = Basic Servo
  Stepper_Motor = Stepper Motor - Unipolar
  Power_Supply = DC Power [voltage=9]
  Gripper_Button = SWITCH-MOMENTARY-2 [package=tactile_switch_tall]
  Ultrasonic = HC-SR04 Ultrasonic Distance Sensor

nets:
  N1: Arduino.D8, cwShoulder.pulse
  N2: Arduino.D9_PWM, Stepper_Motor.A
  N3: Arduino.D10_PWM/SS, Stepper_Motor.B
  N4: Arduino.D11_PWM/MOSI, Stepper_Motor.C
  N5: Arduino.D12/MISO, Stepper_Motor.D
  GND: Arduino.GND, Wrist.gnd, Elbow.gnd, ccwShoulder.gnd, cwShoulder.gnd, Gripper.gnd, Stepper_Motor.COMMON_1, Stepper_Motor.COMMON_2, Power_Supply.V-, Ultrasonic.ECHO
  N6: Arduino.D1/TX, Gripper_Button.2
  N7: Arduino.D2, Ultrasonic.GND
  N8: Arduino.D3_PWM, Ultrasonic.TRIG
  N9: Arduino.D4, Gripper.pulse
  N10: Arduino.D5_PWM, Wrist.pulse
  N11: Arduino.D6_PWM, Elbow.pulse
  N12: Arduino.D7, ccwShoulder.pulse
  VCC: Wrist.vcc, Elbow.vcc, ccwShoulder.vcc, cwShoulder.vcc, Gripper.vcc, Power_Supply.V+, Gripper_Button.1, Ultrasonic.VCC
